# Fritzing sketch workshop1 (saved by Fritzing 0.9.3b)
circuit board: 8.46667cm x 5.64444cm
breadboards: 1

parts:
  Part1 = Adafruit Pro Trinket 5V 16MHz [part_number="Adafruit #2000"]
  R1 = PHOTOCELL [package=photocell]
  SP1 = SPEAKER [package=pcb_mount_speaker]
  U1 = Tri-Color LED SMD [package=led-tricolor-smd]
  Pad1 = Pad [width=1 height=0.69999999999999996 connect=center]  # not connected
  Pad2 = Pad [width=1 height=0.69999999999999996 connect=center]  # not connected
  Pad3 = Pad [width=1 height=0.69999999999999996 connect=center]  # not connected
  Pad4 = Pad [width=1 height=0.69999999999999996 connect=center]  # not connected
  R6 = Resistor [tolerance=±5% resistance=220 package="1206 [SMD]"]
  R3 = Resistor [tolerance=±5% resistance=220 package="1206 [SMD]"]
  R4 = Resistor [tolerance=±5% resistance=220 package="1206 [SMD]"]
  R5 = Resistor [tolerance=±5% resistance=220 package="1206 [SMD]"]

nets:
  N1: Part1.GND, SP1.+, U1.A, R6.Pin_1
  N2: Part1.+5V, R1.P$2
  N3: Part1.D6, R5.Pin_0
  N4: Part1.D5, R4.Pin_0
  N5: Part1.D3, R3.Pin_0
  N6: Part1.D9, SP1.-
  N7: Part1.A0, R1.P$1, R6.Pin_0
  N8: U1.BLU, R3.Pin_1
  N9: U1.GRN, R4.Pin_1
  N10: U1.RED, R5.Pin_1

custom parts:
  Adafruit Pro Trinket 5V 16MHz: Trinket's got a big sister in town - the Pro Trinket 5V! Pro Trinket combines everything you love about Trinket with the familiarity of the common core Arduino chip, the ATmega328. It's like an Arduino Pro Mini with more pins and USB tossed in, so delicious. Trinket's a year old now, and while its been great to see tons of tiny projects, sometimes you just need more pins, more FLASH, and more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

// code stored in the sketch: simple_photosensitive_audio.ino
int photosensorPin = 0;
int piezoPin = 9;

int val = 0;

void setup() {
  pinMode(piezoPin, OUTPUT);
}

void loop() {
  digitalWrite(piezoPin, LOW);
  val = analogRead(photosensorPin);
  val = val/2;

  for( int i=0; i<50; ++i){// play it for 50 cycles
    digitalWrite(piezoPin, HIGH);
    delayMicroseconds(val);
    digitalWrite(piezoPin, LOW);
    delayMicroseconds(val);
  }
}
